# Fritzing sketch blsm-pico (saved by Fritzing 1.0.5)

parts:
  MCU1 = Raspberry Pi Zero
  Mod1 = Raspberry Pi Pico
  J4 = Basic Servo
  J2 = Basic Servo
  J1 = Basic Servo
  Part1 = Adafruit USB Type C Breakout [part_number=4090]
  J3 = Basic Servo
  HC-SR04_Sensor_1 = HC-SR04 Ultrasonic Distance Sensor

nets:
  N1: MCU1.pin_2, MCU1.pin_4, Mod1.pin_39, HC-SR04_Sensor_1.VCC
  N2: MCU1.pin_6, MCU1.pin_9, MCU1.pin_34, MCU1.pin_39, Mod1.pin_3, Mod1.pin_18, Mod1.pin_38, Mod1.pin_42, HC-SR04_Sensor_1.GND
  N3: MCU1.pin_8, Mod1.pin_7
  N4: MCU1.pin_10, Mod1.pin_6
  N5: Mod1.pin_9, J1.pulse
  N6: Mod1.pin_10, J2.pulse
  N7: Mod1.pin_14, J3.pulse
  N8: Mod1.pin_15, J4.pulse
  N9: Mod1.pin_19, HC-SR04_Sensor_1.ECHO
  N10: Mod1.pin_20, HC-SR04_Sensor_1.TRIG
  GND: Mod1.pin_21, J4.gnd, J2.gnd, J1.gnd, Part1.GND, J3.gnd
  VCC: J4.vcc, J2.vcc, J1.vcc, Part1.VBUS, J3.vcc

custom parts:
  Raspberry Pi Pico: Raspberry Pi Pico. Based around the RP2040 microcontroller the Pico is a low cost microcontroller device bringing Raspberry Pi quality, cost, and easy of use to the microcontroller space. Jan 2021, Split part in to two versions: SMD (this one) and tht. This one is single sided and uses the castellation pads to solder the module to the board (no holes, other than for the USB connector!). The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
  Adafruit USB Type C Breakout: Adafruit breakout board for USB Type C socket.
